# Fritzing sketch envsensor (saved by Fritzing 0.9.3b)

parts:
  U2 = NodeMCU V1.0
  Mod1 = CJMCU-811
  Squix1 = OLED 0.96" 128x64 I2C SSD1306

nets:
  N1: U2.D1, Mod1.SCL, Squix1.SCL
  N2: U2.D2, Mod1.SDA, Squix1.SCA
  VCC: U2.3V3, Mod1.VCC, Squix1.VCC
  GND: U2.GND, Mod1.GND, Squix1.GND

custom parts:
  NodeMCU V1.0: ESP8266 based NodeMCU
  CJMCU-811: The CCS811 is an ultra-low power digital gas sensor solution which integrates a metal oxide (MOX) gas sensor to detect a wide range of Volatile Organic Compounds (VOCs) for indoor air quality monitoring with a microcontroller unit (MCU), which includes an Analog-to-Digital converter (ADC), and an I²C interface.
